# Fritzing sketch Schematic (saved by Fritzing 0.9.3b)
breadboards: 1

parts:
  U1 = atmega168 [package=dip]
  LCD1 = LCD screen
  S1 = Pushbutton [package="[SMD]"]
  S2 = Pushbutton [package="[SMD]"]
  S3 = Pushbutton [package="[SMD]"]
  S4 = Pushbutton [package="[SMD]"]

nets:
  VCC: U1.VCC, LCD1.VDD
  N1: U1.GND#7, LCD1.VSS
  N2: U1.XLAT1, LCD1.DB6
  N3: U1.XLAT2, LCD1.DB7
  N4: U1.D8, LCD1.DB0
  N5: U1.D9_(PWM), LCD1.DB1
  N6: U1.D10_(PWM), LCD1.DB2
  N7: U1.D11_(PWM), LCD1.DB3
  N8: U1.D12, LCD1.DB4
  N9: U1.D13, LCD1.DB5
  N10: S1.Pin_1, S1.Pin_2
  N11: S1.Pin_3, S1.Pin_4
  N12: S2.Pin_1, S2.Pin_2
  N13: S2.Pin_3, S2.Pin_4
  N14: S3.Pin_1, S3.Pin_2
  N15: S3.Pin_3, S3.Pin_4
  N16: S4.Pin_1, S4.Pin_2
  N17: S4.Pin_3, S4.Pin_4
